// Logisim project summator.circ as structural Verilog: 2 circuits, main circuit main
module main (
  input  [7:0] in_1,
  input  [7:0] in_2,
  output [7:0] out_3,
  output out_4
);

  wire ods_1_bit_1_p_out, ods_1_bit_2_p_out, ods_1_bit_3_p_out, ods_1_bit_4_p_out, ods_1_bit_5_p_out,
       ods_1_bit_6_p_out, ods_1_bit_7_p_out;

  ODS_1_bit ods_1_bit_1 (.X1(in_1[0]), .X2(in_2[0]), .X3(1'b0), .S(out_3[0]), .P_out(ods_1_bit_1_p_out));
  ODS_1_bit ods_1_bit_2 (.X1(in_1[1]), .X2(in_2[1]), .X3(ods_1_bit_1_p_out), .S(out_3[1]), .P_out(ods_1_bit_2_p_out));
  ODS_1_bit ods_1_bit_3 (.X1(in_1[2]), .X2(in_2[2]), .X3(ods_1_bit_2_p_out), .S(out_3[2]), .P_out(ods_1_bit_3_p_out));
  ODS_1_bit ods_1_bit_4 (.X1(in_1[3]), .X2(in_2[3]), .X3(ods_1_bit_3_p_out), .S(out_3[3]), .P_out(ods_1_bit_4_p_out));
  ODS_1_bit ods_1_bit_5 (.X1(in_1[4]), .X2(in_2[4]), .X3(ods_1_bit_4_p_out), .S(out_3[4]), .P_out(ods_1_bit_5_p_out));
  ODS_1_bit ods_1_bit_6 (.X1(in_1[5]), .X2(in_2[5]), .X3(ods_1_bit_5_p_out), .S(out_3[5]), .P_out(ods_1_bit_6_p_out));
  ODS_1_bit ods_1_bit_7 (.X1(in_1[6]), .X2(in_2[6]), .X3(ods_1_bit_6_p_out), .S(out_3[6]), .P_out(ods_1_bit_7_p_out));
  ODS_1_bit ods_1_bit_8 (.X1(in_1[7]), .X2(in_2[7]), .X3(ods_1_bit_7_p_out), .S(out_3[7]), .P_out(out_4));
endmodule

module ODS_1_bit (
  input  X1,
  input  X2,
  input  X3,
  output S,
  output P_out
);

  wire and_1_out, and_2_out, and_3_out, and_4_out, and_5_out, and_6_out, and_7_out, and_8_out, not_1_out,
       not_2_out, not_3_out;

  not not_1 (not_1_out, X1);
  not not_2 (not_2_out, X2);
  not not_3 (not_3_out, X3);
  and and_1 (and_1_out, not_1_out, not_2_out, X3);
  and and_2 (and_2_out, not_1_out, X2, not_3_out);
  and and_3 (and_3_out, X1, not_2_out, not_3_out);
  and and_4 (and_4_out, X1, X2, X3);
  and and_5 (and_5_out, not_1_out, X2, X3);
  and and_6 (and_6_out, X1, not_2_out, X3);
  and and_7 (and_7_out, X1, X2, not_3_out);
  and and_8 (and_8_out, X1, X2, X3);
  or or_1 (S, and_1_out, and_2_out, and_3_out, and_4_out);
  or or_2 (P_out, and_5_out, and_6_out, and_7_out, and_8_out);
endmodule
